// Logisim project Full_CPU.circ as structural Verilog: 8 circuits, main circuit main
module main (
);

  wire clock_1_out, cpu_1_mem_read, cpu_1_mem_write, RESET_out;
  wire [7:0] cpu_1_address;
  wire [31:0] cpu_1_data_to_mem, ram_1_data;

  Button RESET (.out(RESET_out));
  CPU cpu_1 (
    .Clock(clock_1_out), .Reset(RESET_out), .Mem_Read(cpu_1_mem_read), .Mem_Write(cpu_1_mem_write),
    .Data_From_Mem(ram_1_data), .Address(cpu_1_address), .Data_To_Mem(cpu_1_data_to_mem));
  Clock clock_1 (.out(clock_1_out));
  RAM #(.dataWidth(32), .bus("separate")) ram_1 (
    .addr(cpu_1_address), .din(cpu_1_data_to_mem), .data(ram_1_data), .str(cpu_1_mem_write),
    .clk(clock_1_out), .ld(cpu_1_mem_read), .clr(RESET_out));  // open: sel

  // Notes on the sheet:
  //   Fully Functional CPU (Highest Abstraction)
  //   19CS02012
  //   Sushant Kumar
endmodule

module CPU (
  input  Clock,
  input  [31:0] Data_From_Mem,
  input  Reset,
  output Mem_Read,
  output Mem_Write,
  output [7:0] Address,
  output [31:0] Data_To_Mem
);

  wire and_1_out, control_unit_1_cpu_enable, control_unit_1_ir_en, control_unit_1_ir_muxy_sel,
       control_unit_1_muxa, control_unit_1_muxy, control_unit_1_pc_inc, control_unit_1_pc_rz_sel,
       control_unit_1_ra_en, control_unit_1_rb_en, control_unit_1_rm_en, control_unit_1_ry_en,
       control_unit_1_rz_en, control_unit_1_write;
  wire [1:0] control_unit_1_inst_sel, control_unit_1_muxb;
  wire [2:0] decode_1_dest, decode_1_src1, decode_1_src2;
  wire [3:0] decode_1_op_code;
  wire [31:0] alu_1_alu_out, decode_1_muxb, gprs_register_file_1_a_out, gprs_register_file_1_b_out, IR_q,
       memory_interface_1_ir, memory_interface_1_muxy, multiplexer_1_out, multiplexer_2_out,
       multiplexer_3_out, program_counter_1_pc_val, Ra_q, Rb_q, Rm_q, Ry_q, Rz_q;

  and and_1 (and_1_out, control_unit_1_cpu_enable, Clock);
  GPRS_Register_FIle gprs_register_file_1 (
    .Write(control_unit_1_write), .Input_select(decode_1_dest), .Input_Data(Ry_q), .Clock(and_1_out),
    .Reset(Reset), .A_out(gprs_register_file_1_a_out), .A_Addr(decode_1_src1),
    .B_out(gprs_register_file_1_b_out), .B_Addr(decode_1_src2));
  ALU alu_1 (
    .Inst_select(control_unit_1_inst_sel), .ALU_OUT(alu_1_alu_out), .In_A(multiplexer_1_out),
    .In_B(multiplexer_2_out));
  Register #(.width(32)) Ra (
    .D(gprs_register_file_1_a_out), .en(control_unit_1_ra_en), .Q(Ra_q), .clk(and_1_out), .clr(Reset));
  Multiplexer #(.width(32), .enable("false")) multiplexer_1 (
    .in0(Ra_q), .in1({32{1'b0}}), .out(multiplexer_1_out), .sel(control_unit_1_muxa));
  Register #(.width(32)) Rb (
    .D(gprs_register_file_1_b_out), .en(control_unit_1_rb_en), .Q(Rb_q), .clk(and_1_out), .clr(Reset));
  Multiplexer #(.select(2), .width(32), .enable("false")) multiplexer_2 (
    .in0(Rb_q), .in1(decode_1_muxb), .in2({32{1'b0}}), .out(multiplexer_2_out), .sel(control_unit_1_muxb));  // open: in3
  Register #(.width(32)) Rz (.D(alu_1_alu_out), .en(control_unit_1_rz_en), .Q(Rz_q), .clk(and_1_out), .clr(Reset));
  Multiplexer #(.width(32), .enable("false")) multiplexer_3 (
    .in0(Rz_q), .in1(memory_interface_1_muxy), .out(multiplexer_3_out), .sel(control_unit_1_muxy));
  Decode decode_1 (
    .IR(IR_q), .Op_code(decode_1_op_code), .dest(decode_1_dest), .src2(decode_1_src2), .muxB(decode_1_muxb),
    .src1(decode_1_src1));
  Register #(.width(32)) Ry (.D(multiplexer_3_out), .en(control_unit_1_ry_en), .Q(Ry_q), .clk(and_1_out), .clr(Reset));
  Program_Counter program_counter_1 (
    .Clock(and_1_out), .Reset(Reset), .PC_Inc(control_unit_1_pc_inc), .PC_val(program_counter_1_pc_val));
  Register #(.width(32)) Rm (.D(Rb_q), .en(control_unit_1_rm_en), .Q(Rm_q), .clk(and_1_out), .clr(Reset));
  Register #(.width(32)) IR (
    .D(memory_interface_1_ir), .en(control_unit_1_ir_en), .Q(IR_q), .clk(and_1_out), .clr(Reset));
  Memory_Interface memory_interface_1 (
    .Data_In_From_Mem(Data_From_Mem), .IR_muxY_Sel(control_unit_1_ir_muxy_sel), .Rz(Rz_q),
    .PC_val(program_counter_1_pc_val), .PC_Rz_Sel(control_unit_1_pc_rz_sel), .Rm(Rm_q),
    .IR(memory_interface_1_ir), .muxY(memory_interface_1_muxy), .out_9(Address), .Data_Out_To_Mem(Data_To_Mem));
  Control_Unit control_unit_1 (
    .Op_code(decode_1_op_code), .Clock(and_1_out), .Reset(Reset), .CPU_Enable(control_unit_1_cpu_enable),
    .IR_muxY_Sel(control_unit_1_ir_muxy_sel), .muxY(control_unit_1_muxy), .Pc_Inc(control_unit_1_pc_inc),
    .Pc_Rz_Sel(control_unit_1_pc_rz_sel), .Mem_Read(Mem_Read), .IR_En(control_unit_1_ir_en),
    .Mem_Write(Mem_Write), .Ra_En(control_unit_1_ra_en), .Rb_En(control_unit_1_rb_en),
    .Rz_En(control_unit_1_rz_en), .Rm_En(control_unit_1_rm_en), .Ry_En(control_unit_1_ry_en),
    .muxA(control_unit_1_muxa), .Write(control_unit_1_write), .muxB(control_unit_1_muxb),
    .Inst_Sel(control_unit_1_inst_sel));

  // Notes on the sheet:
  //   Full Five Stage CPU Implementation
  //   19CS02012
  //   Sushant Kumar
endmodule

module ALU (
  input  [31:0] In_A,
  input  [31:0] In_B,
  input  [1:0] Inst_select,
  output [31:0] ALU_OUT
);

  wire [31:0] adder_1_out, and_1_out, or_1_out, subtractor_1_out;

  Adder #(.width(32)) adder_1 (.a(In_A), .b(In_B), .out(adder_1_out));  // open: cin, cout
  Subtractor #(.width(32)) subtractor_1 (.a(In_A), .b(In_B), .out(subtractor_1_out));  // open: bin, bout
  assign and_1_out = In_A & In_B;  // AND_Gate and_1, 32 bits wide
  assign or_1_out = In_A | In_B;  // OR_Gate or_1, 32 bits wide
  Multiplexer #(.select(2), .width(32)) multiplexer_1 (
    .in0(adder_1_out), .in1(subtractor_1_out), .in2(and_1_out), .in3(or_1_out), .out(ALU_OUT),
    .sel(Inst_select));  // open: en

  // Notes on the sheet:
  //   ALU Internal Implementation
  //   Sushant Kumar
  //   19CS02012
  //   00 - Add
  //   01 - Sub
  //   10 - AND
  //   11 - OR
endmodule

module GPRS_Register_FIle (
  input  Write,
  input  [2:0] A_Addr,
  input  [2:0] Input_select,
  input  [31:0] Input_Data,
  input  Clock,
  input  [2:0] B_Addr,
  input  Reset,
  output [31:0] A_out,
  output [31:0] B_out
);

  wire decoder_1_out0, decoder_1_out1, decoder_1_out2, decoder_1_out3, decoder_1_out4, decoder_1_out5,
       decoder_1_out6, decoder_1_out7;
  wire [31:0] register_1_q, register_2_q, register_3_q, register_4_q, register_5_q, register_6_q,
       register_7_q, register_8_q;

  Decoder #(.select(3), .disabled(0)) decoder_1 (
    .out0(decoder_1_out0), .out1(decoder_1_out1), .out2(decoder_1_out2), .out3(decoder_1_out3),
    .out4(decoder_1_out4), .out5(decoder_1_out5), .out6(decoder_1_out6), .out7(decoder_1_out7),
    .sel(Input_select), .en(Write));
  Register #(.width(32)) register_1 (.D(Input_Data), .en(decoder_1_out0), .Q(register_1_q), .clk(Clock), .clr(Reset));
  Register #(.width(32)) register_2 (.D(Input_Data), .en(decoder_1_out1), .Q(register_2_q), .clk(Clock), .clr(Reset));
  Register #(.width(32)) register_3 (.D(Input_Data), .en(decoder_1_out2), .Q(register_3_q), .clk(Clock), .clr(Reset));
  Register #(.width(32)) register_4 (.D(Input_Data), .en(decoder_1_out3), .Q(register_4_q), .clk(Clock), .clr(Reset));
  Register #(.width(32)) register_5 (.D(Input_Data), .en(decoder_1_out4), .Q(register_5_q), .clk(Clock), .clr(Reset));
  Register #(.width(32)) register_6 (.D(Input_Data), .en(decoder_1_out5), .Q(register_6_q), .clk(Clock), .clr(Reset));
  Register #(.width(32)) register_7 (.D(Input_Data), .en(decoder_1_out6), .Q(register_7_q), .clk(Clock), .clr(Reset));
  Register #(.width(32)) register_8 (.D(Input_Data), .en(decoder_1_out7), .Q(register_8_q), .clk(Clock), .clr(Reset));
  Multiplexer #(.select(3), .width(32), .disabled(0)) multiplexer_1 (
    .in0(register_1_q), .in1(register_2_q), .in2(register_3_q), .in3(register_4_q), .in4(register_5_q),
    .in5(register_6_q), .in6(register_7_q), .in7(register_8_q), .out(A_out), .sel(A_Addr), .en(1'b1));
  Multiplexer #(.select(3), .width(32), .disabled(0)) multiplexer_2 (
    .in0(register_1_q), .in1(register_2_q), .in2(register_3_q), .in3(register_4_q), .in4(register_5_q),
    .in5(register_6_q), .in6(register_7_q), .in7(register_8_q), .out(B_out), .sel(B_Addr), .en(1'b1));

  // Notes on the sheet:
  //   GPRS_Register_File_Internal_Implementation
  //   19CS02012
  //   Sushant Kumar
endmodule

module Program_Counter (
  input  Clock,
  input  Reset,
  input  PC_Inc,
  output [31:0] PC_val
);

  wire [31:0] adder_1_out, multiplexer_1_out;

  Register #(.width(32)) register_1 (.D(multiplexer_1_out), .Q(PC_val), .clk(Clock), .clr(Reset));  // open: en
  Multiplexer #(.width(32)) multiplexer_1 (
    .in0(PC_val), .in1(adder_1_out), .out(multiplexer_1_out), .sel(PC_Inc));  // open: en
  Adder #(.width(32)) adder_1 (.a(PC_val), .b(32'h1), .out(adder_1_out));  // open: cin, cout

  // Notes on the sheet:
  //   PC Internal Implementation
  //   19CS02012
  //   Sushant Kumar
endmodule

module Memory_Interface (
  input  [31:0] Data_In_From_Mem,
  input  IR_muxY_Sel,
  input  [31:0] Rz,
  input  [31:0] PC_val,
  input  PC_Rz_Sel,
  input  [31:0] Rm,
  output [31:0] IR,
  output [31:0] muxY,
  output [7:0] out_9,
  output [31:0] Data_Out_To_Mem
);

  wire [31:8] multiplexer_1_out;

  Demultiplexer #(.width(32)) demultiplexer_1 (
    .out0(IR), .out1(muxY), .in(Data_In_From_Mem), .sel(IR_muxY_Sel));  // open: en
  Multiplexer #(.width(32)) multiplexer_1 (
    .in0(Rz), .in1(PC_val), .out({multiplexer_1_out, out_9}), .sel(PC_Rz_Sel));  // open: en

  assign Data_Out_To_Mem = Rm;

  // Notes on the sheet:
  //   Processor Memory Interface Internal Implementation
  //   19CS02012
  //   Sushant Kumar
endmodule

module Decode (
  input  [31:0] IR,
  output [31:0] muxB,
  output [2:0] src2,
  output [2:0] src1,
  output [2:0] dest,
  output [3:0] Op_code
);

  assign muxB = {{16{1'b0}}, IR[15:0]};  // Bit_Extender bit_extender_1

  assign dest = IR[27:25];
  assign Op_code = IR[31:28];
  assign src1 = IR[24:22];
  assign src2 = IR[21:19];

  // Notes on the sheet:
  //   Bits Separator Internal Implementation
  //   19CS02012
  //   Sushant Kumar
endmodule

module Control_Unit (
  input  [3:0] Op_code,
  input  Clock,
  input  Reset,
  output [1:0] muxB,
  output CPU_Enable,
  output IR_muxY_Sel,
  output muxY,
  output Pc_Inc,
  output Pc_Rz_Sel,
  output Mem_Read,
  output IR_En,
  output Mem_Write,
  output [1:0] Inst_Sel,
  output Ra_En,
  output Rb_En,
  output Rz_En,
  output Rm_En,
  output Ry_En,
  output muxA,
  output Write
);

  wire and_1_out, decoder_1_out1, decoder_1_out3, decoder_1_out4, decoder_2_out1, decoder_2_out2,
       decoder_2_out3, decoder_2_out4, decoder_2_out5, decoder_2_out6, decoder_2_out7, decoder_2_out8,
       decoder_2_out9, decoder_2_out10, decoder_2_out11, decoder_2_out12, not_1_out, not_2_out, not_4_out,
       not_5_out, not_6_out, not_7_out, or_4_out;
  wire [2:0] counter_1_q;

  or or_1 (Inst_Sel[1], decoder_2_out8, decoder_2_out9, decoder_2_out10, decoder_2_out11);
  or or_2 (Inst_Sel[0], decoder_2_out6, decoder_2_out7, decoder_2_out10, decoder_2_out11);
  or or_3 (muxB[0], decoder_2_out1, decoder_2_out2, decoder_2_out3, decoder_2_out5, decoder_2_out7, decoder_2_out9, decoder_2_out11);
  Decoder #(.select(3), .enable("false")) decoder_1 (
    .out0(IR_En), .out1(decoder_1_out1), .out2(Rz_En), .out3(decoder_1_out3), .out4(decoder_1_out4),
    .sel(counter_1_q));  // open: out5, out6, out7
  Counter #(.width(3), .max('h4)) counter_1 (.Q(counter_1_q), .clk(Clock), .clr(Reset));  // open: load, D, count, carry
  Decoder #(.select(4), .enable("false")) decoder_2 (
    .out0(muxB[1]), .out1(decoder_2_out1), .out2(decoder_2_out2), .out3(decoder_2_out3),
    .out4(decoder_2_out4), .out5(decoder_2_out5), .out6(decoder_2_out6), .out7(decoder_2_out7),
    .out8(decoder_2_out8), .out9(decoder_2_out9), .out10(decoder_2_out10), .out11(decoder_2_out11),
    .out12(decoder_2_out12), .sel(Op_code));  // open: out13, out14, out15
  and and_1 (and_1_out, decoder_1_out3, decoder_2_out2);
  and and_2 (Mem_Write, decoder_1_out3, decoder_2_out3);
  not not_1 (not_1_out, decoder_2_out3);
  not not_2 (not_2_out, decoder_2_out12);
  not not_3 (CPU_Enable, decoder_2_out12);
  and and_3 (IR_muxY_Sel, decoder_2_out2, decoder_1_out3);
  not not_4 (not_4_out, decoder_2_out1);
  not not_5 (not_5_out, decoder_2_out12);
  or or_4 (or_4_out, decoder_2_out10, decoder_2_out8, decoder_2_out6, decoder_2_out4, decoder_2_out3);
  not not_6 (not_6_out, decoder_2_out3);
  and and_4 (Ry_En, not_6_out, decoder_1_out3, not_7_out);
  not not_7 (not_7_out, decoder_2_out12);
  or or_5 (Mem_Read, IR_En, and_1_out);
  and and_5 (Ra_En, decoder_1_out1, not_4_out, not_5_out);
  and and_6 (Rm_En, Rz_En, decoder_2_out3);
  and and_7 (muxA, decoder_2_out1, Rz_En);
  and and_8 (Write, not_1_out, not_2_out, decoder_1_out4);
  and and_9 (Rb_En, decoder_1_out1, or_4_out);

  assign muxY = IR_muxY_Sel;
  assign Pc_Inc = IR_En;
  assign Pc_Rz_Sel = IR_En;

  // Notes on the sheet:
  //   19CS02012
  //   Sushant Kumar
  //   Control Unit Internal Implementation
endmodule
